# Fritzing sketch easydriverboard_groundfill (saved by Fritzing 0.9.10b)
circuit board: 7.59221cm x 9.7916cm
breadboards: 1

parts:
  Part1 = EasyDriver_v44
  J1 = female pin header, 4 pins [form="♀ (female)"]
  J2 = female pin header, 3 pins [form="♀ (female)"]
  Part2 = EasyDriver_v44
  J3 = female pin header, 4 pins [form="♀ (female)"]
  Part3 = EasyDriver_v44
  Part4 = EasyDriver_v44
  J4 = female pin header, 4 pins [form="♀ (female)"]
  J5 = female pin header, 4 pins [form="♀ (female)"]
  J6 = female pin header, 3 pins [form="♀ (female)"]
  J7 = female pin header, 3 pins [form="♀ (female)"]
  J8 = female pin header, 3 pins [form="♀ (female)"]
  J9 = female pin header, 2 pins [form="♀ (female)"]
  J10 = female pin header, 2 pins [form="♀ (female)"]
  C1 = Electrolytic Capacitor [capacitance=1µF voltage=35V package="100 mil [THT, electrolytic]"]
  J11 = female pin header, 4 pins [form="♀ (female)"]
  J12 = female pin header, 2 pins [form="♀ (female)"]
  J13 = female pin header, 2 pins [form="♀ (female)"]

nets:
  GND: Part1.GND, Part2.GND, Part3.GND, Part4.GND, J9.pin1, J9.pin2, C1.-, J11.pin1, J11.pin2, J11.pin3, J11.pin4, J12.pin1, J13.pin1
  N1: Part1.V+, Part2.V+, Part3.V+, Part4.V+, J10.pin1, J10.pin2, C1.+
  N2: Part1.STEP, J2.pin2
  N3: Part1.DIR, J2.pin3
  N4: Part1.OUT2A, J1.pin1
  N5: Part1.OUT2B, J1.pin2
  N6: Part1.OUT1A, J1.pin3
  N7: Part1.OUT1B, J1.pin4
  VCC: Part1.VCC, Part2.VCC, Part3.VCC, Part4.VCC, J12.pin2, J13.pin2
  N8: Part1.ENABLE, J2.pin1
  N9: Part2.STEP, J6.pin2
  N10: Part2.DIR, J6.pin3
  N11: Part2.OUT2A, J3.pin1
  N12: Part2.OUT2B, J3.pin2
  N13: Part2.OUT1A, J3.pin3
  N14: Part2.OUT1B, J3.pin4
  N15: Part2.ENABLE, J6.pin1
  N16: Part3.STEP, J7.pin2
  N17: Part3.DIR, J7.pin3
  N18: Part3.OUT2A, J5.pin1
  N19: Part3.OUT2B, J5.pin2
  N20: Part3.OUT1A, J5.pin3
  N21: Part3.OUT1B, J5.pin4
  N22: Part3.ENABLE, J7.pin1
  N23: Part4.STEP, J8.pin2
  N24: Part4.DIR, J8.pin3
  N25: Part4.OUT2A, J4.pin1
  N26: Part4.OUT2B, J4.pin2
  N27: Part4.OUT1A, J4.pin3
  N28: Part4.OUT1B, J4.pin4
  N29: Part4.ENABLE, J8.pin1

notes:
  GND
  12V
  EN
  STEP
  DIR
  Stepper drivers v1
  Marius Krabset 2023
  5V
