# Fritzing sketch easydriverboard_x3 (saved by Fritzing 0.9.10b)
circuit board: 6.90547cm x 7.35508cm
breadboards: 1

parts:
  Part1 = EasyDriver_v44
  J1 = female pin header, 4 pins [form="♀ (female)"]
  J2 = female pin header, 3 pins [form="♀ (female)"]
  J9 = female pin header, 2 pins [form="♀ (female)"]
  J10 = female pin header, 2 pins [form="♀ (female)"]
  Part2 = EasyDriver_v44
  J11 = female pin header, 3 pins [form="♀ (female)"]
  J12 = female pin header, 4 pins [form="♀ (female)"]
  Part3 = EasyDriver_v44
  J13 = female pin header, 3 pins [form="♀ (female)"]
  J14 = female pin header, 4 pins [form="♀ (female)"]
  J15 = female pin header, 2 pins [form="♀ (female)"]

nets:
  GND: Part1.GND, J9.pin1, J9.pin2, Part2.GND, Part3.GND, J15.pin1, J15.pin2
  N1: Part1.V+, J10.pin1, J10.pin2, Part2.V+, Part3.V+
  N2: Part1.STEP, J2.pin2
  N3: Part1.DIR, J2.pin3
  N4: Part1.OUT2A, J1.pin1
  N5: Part1.OUT2B, J1.pin2
  N6: Part1.OUT1A, J1.pin3
  N7: Part1.OUT1B, J1.pin4
  N8: Part1.ENABLE, J2.pin1
  N9: Part2.STEP, J11.pin2
  N10: Part2.DIR, J11.pin3
  N11: Part2.OUT2A, J12.pin1
  N12: Part2.OUT2B, J12.pin2
  N13: Part2.OUT1A, J12.pin3
  N14: Part2.OUT1B, J12.pin4
  N15: Part2.ENABLE, J11.pin1
  N16: Part3.STEP, J13.pin2
  N17: Part3.DIR, J13.pin3
  N18: Part3.OUT2A, J14.pin1
  N19: Part3.OUT2B, J14.pin2
  N20: Part3.OUT1A, J14.pin3
  N21: Part3.OUT1B, J14.pin4
  N22: Part3.ENABLE, J13.pin1

notes:
  GND
  12V
  EN
  STEP
  DIR
  Stepper drivers 3x v1
  Marius Krabset 2023
